// Logisim project control-logic.circ as structural Verilog: 1 circuit, main circuit control_logic
module control_logic (
  input  [31:0] Instruction,
  input  BrEq,
  input  BrLt,
  output PCSel,
  output RegWEn,
  output [2:0] ImmSel,
  output BrUn,
  output ASel,
  output BSel,
  output [3:0] ALUSel,
  output MemWEn,
  output [1:0] WBSel
);

  wire and_2_out, and_3_out, comparator_1_eq, comparator_2_eq, comparator_3_eq, comparator_4_eq, op33;
  wire [2:0] bit_extender_1_out;
  wire [3:0] multiplexer_1_out;
  wire [3:3] and_1_out;
  wire [15:0] rom_1_data;

  and and_1 (and_1_out[3], Instruction[25], op33);
  Comparator #(.mode("unsigned"), .width(7)) comparator_1 (
    .a(Instruction[6:0]), .b(7'b0010011), .eq(comparator_1_eq));  // open: gt, lt
  Comparator #(.mode("unsigned"), .width(7)) comparator_2 (
    .a(Instruction[6:0]), .b(7'b0110011), .eq(comparator_2_eq));  // open: gt, lt
  buf buffer_1 (op33, comparator_2_eq);
  ROM #(.addrWidth(6), .dataWidth(16)) rom_1 (.data(rom_1_data));  // open: addr
  buf buffer_2 (RegWEn, comparator_1_eq);
  assign bit_extender_1_out = {{2{comparator_1_eq}}, comparator_1_eq};  // Bit_Extender bit_extender_1
  Comparator #(.mode("unsigned"), .width(7)) comparator_3 (
    .a(Instruction[31:25]), .b(7'b0100000), .eq(comparator_3_eq));  // open: gt, lt
  Comparator #(.mode("unsigned"), .width(3)) comparator_4 (
    .a(Instruction[14:12]), .b(3'b000), .eq(comparator_4_eq));  // open: gt, lt
  buf buffer_3 (RegWEn, comparator_2_eq);
  not not_1 (BSel, comparator_2_eq);
  assign ImmSel = ~bit_extender_1_out;  // NOT_Gate not_2, 3 bits wide
  Multiplexer #(.width(4)) multiplexer_1 (.in0(4'b1101), .in1(4'b1100), .out(multiplexer_1_out), .sel(and_2_out));
  and and_2 (and_2_out, comparator_3_eq, comparator_4_eq);
  Multiplexer #(.width(4)) multiplexer_2 (
    .in0({and_1_out[3], Instruction[14:12]}), .in1(multiplexer_1_out), .out(ALUSel), .sel(and_3_out));
  and and_3 (and_3_out, and_2_out, op33);

  // Other names for the same wires on the sheet: func3[2:0] = Instruction[14:12]; OpCode[6:0] = Instruction[6:0];
  //   func7[6:0] = Instruction[31:25]

  // Notes on the sheet:
  //   INPUTS to your circuit
  //   Connect ROM Input here ->
  //   ROM FOR CONTROL LOGIC
  //   DON'T CHANGE THE LOCATIONS OF THE INPUTS AND OUTPUTS!
  //   This is only if you choose to do the ROM option
  //   CONNECT
  //   WIRE
  //   TO
  //   USE
  //   ROM
  //   OUTPUT from your circuit
  //   Reminder: If using ROM, use combinational logic for PCSel
endmodule
